// Logisim project comparator.circ as structural Verilog: 1 circuit, main circuit main
module main (
  input  in_1,
  input  a,
  input  in_3,
  input  b,
  input  in_5,
  input  c,
  input  in_7,
  input  d
);

  wire and_1_out, and_2_out, and_3_out, not_1_out, not_2_out, not_3_out, not_4_out;

  not not_1 (not_1_out, in_3);
  not not_2 (not_2_out, in_7);
  and and_1 (and_1_out, in_1, not_1_out, in_5, not_2_out);
  and and_2 (and_2_out, and_1_out, and_3_out);
  // Probe on and_2_out
  and and_3 (and_3_out, a, not_3_out, c, not_4_out);
  not not_3 (not_3_out, b);
  not not_4 (not_4_out, d);

  // Notes on the sheet:
  //   Compare Against
  //   1010
  //   input address
endmodule
