// Logisim project comparatorlut.circ as structural Verilog: 1 circuit, main circuit main
module main (
  input  _7,
  input  PADDR,
  input  in_3,
  input  _3,
  input  in_5,
  input  in_6,
  input  _0,
  input  in_8
);

  wire rom_3_data;
  wire [1:0] rom_1_data;

  ROM #(.addrWidth(5), .dataWidth(1)) rom_1 (.addr({in_5, _3, in_3, PADDR, _7}), .data(rom_1_data[0]));  // open: sel
  ROM #(.addrWidth(5), .dataWidth(1)) rom_2 (.addr({in_5, _3, in_3, PADDR, _7}), .data(rom_1_data[1]));  // open: sel
  // Probe on rom_1_data[0]
  // Probe on rom_1_data[1]
  ROM #(.addrWidth(5), .dataWidth(1)) rom_3 (.addr({3'b000, rom_1_data}), .data(rom_3_data));  // open: sel
  // Probe on rom_3_data

  // Notes on the sheet:
  //   LUT PSEL Peripheral A 0xA0
  //   LUT PSEL Peripheral B 0xF0
  //   contents of rom_1 (hex, n*v repeats v):
  //   5*0 1
  //   contents of rom_2 (hex, n*v repeats v):
  //   15*0 1
  //   PSEL A
  //   PSEL B
  //   LUT PSEL Default (error case)
  //   contents of rom_3 (hex, n*v repeats v):
  //   1
  //   PSEL Default
endmodule
